# Fritzing sketch ProtoStax_Air_Quality_Monitor (saved by Fritzing 0.9.3b)
breadboards: 1

parts:
  J1 = Basic Servo
  LED1 = RGB LED - (4 legs) [package="5 mm [THT]"]
  R1 = Resistor [tolerance=±5% resistance=100 package="1206 [SMD]"]
  R2 = Resistor [tolerance=±5% resistance=100 package="1206 [SMD]"]
  R4 = Resistor [tolerance=±5% resistance=430 package=THT]
  R5 = Resistor [tolerance=±5% resistance=10k package=THT]
  Raspberry_Pi1 = Raspberry Pi B+

nets:
  GND: J1.gnd, R5.Pin_1, Raspberry_Pi1.GND
  VCC: J1.vcc, Raspberry_Pi1.5V
  N1: J1.pulse, R5.Pin_0, Raspberry_Pi1.GPIO4
  N2: LED1.red_cathode, R4.Pin_0
  N3: LED1.common_anode, Raspberry_Pi1.3v3
  N4: LED1.green_cathode, R2.Pin_0
  N5: LED1.blue_cathode, R1.Pin_0
  N6: R1.Pin_1, Raspberry_Pi1.GPIO22
  N7: R2.Pin_1, Raspberry_Pi1.GPIO27
  N8: R4.Pin_1, Raspberry_Pi1.GPIO17
